# Fritzing sketch Rangkaian (saved by Fritzing 0.9.2b)

parts:
  Part1 = Arduino Mega ADK (Rev3)
  Part2 = RFID-RC522-v2
  Keypad4x1 = Keypad Membran 4x4
  ZS-042_RTC1 = ZS-042 RTC Module
  Display1 = LCD screen 16x2 IIC [part_number=101290]
  U1 = NodeMCU V3.0
  J1 = Basic Servo
  J2 = Basic Servo
  J3 = Basic Servo
  Part4 = Thermal Printer
  SP1 = SPEAKER [package=pcb_mount_speaker]
  DFPlayer_Mini1 = DFPlayer MINI [package="DIP (Dual Inline) [THT]"]

nets:
  N1: Part1.D21/SCL, ZS-042_RTC1.SCL, Display1.SCL
  N2: Part1.D20/SDA, ZS-042_RTC1.SDA, Display1.SDA
  N3: Part1.D19/RX1, Part4.RXD
  N4: Part1.D18/TX1, Part4.TXD
  N5: Part1.D17/RX2, DFPlayer_Mini1.TX
  N6: Part1.D16/TX2, DFPlayer_Mini1.RX
  N7: Part1.D13_PWM, J1.pulse
  N8: Part1.D12_PWM, J2.pulse
  N9: Part1.D11_PWM, J3.pulse
  3V3: Part1.3V3, Part2.3.3V
  N10: Part1.D0/RX0, U1.RX
  N11: Part1.D1/TX0, U1.TX
  N12: Part1.D5_PWM, Part2.RST
  5V: Part1.5V, Display1.VCC
  N13: Part1.D23, Keypad4x1.Pin1
  N14: Part1.D25, Keypad4x1.Pin2
  N15: Part1.D27, Keypad4x1.Pin3
  N16: Part1.D29, Keypad4x1.Pin4
  N17: Part1.D31, Keypad4x1.Pin5
  N18: Part1.D33, Keypad4x1.Pin6
  N19: Part1.D35, Keypad4x1.Pin7
  N20: Part1.D37, Keypad4x1.Pin8
  N21: Part1.D49, Part2.SDA
  N22: Part1.D50/MISO, Part2.MISO
  N23: Part1.D51/MOSI, Part2.MOSI
  N24: Part1.D52/SCK, Part2.SCK
  N25: Part1.D53/SS, Part2.GND
  GND: Part1.GND, Display1.GND
  N26: SP1.+, DFPlayer_Mini1.SPK2
  N27: SP1.-, DFPlayer_Mini1.SPK1

custom parts:
  RFID-RC522-v2: A simple China made RFID-RC522 Reader; do check the pin labels, as this is a MFRC522 based clone.
  Keypad Membran 4x4: Membrane Keypad 4x4 Matrix
  LCD screen 16x2 IIC: LCD screen with HD44780 controller enables showing text, symbols, value or anything else that comes from Croduino/Arduino. It is capable of showing 16 symbols in two lines and therefore can be used in many projects that need to send clearly visible and legible output information.. • Color of symbols: White • Backlight: Blue • Dimensions: 80 x 36 x 12 mm • Screen dimensions: 64.5 x 16 mm •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
  NodeMCU V3.0: ESP8266 based NodeMCU
  DFPlayer MINI: MP3 module by DFRobot.com for playing Music from an SD-Card. Supports WAV and MP3 files.
